// Digital circuit 2.dig as structural Verilog
module _2 (
  input  I_0,
  input  T_1,
  input  T_2,
  input  I_1,
  input  I_2,
  input  I_3,
  input  S_0,
  input  S_1,
  input  S_2,
  input  T_0,
  input  Adr_0,
  input  Adr_1,
  input  Adr_2,
  input  Adr_3,
  output O_0,
  output O_1,
  output O_2,
  output O_3
);

  wire Clock, nand_1_out, RAM_0, RAM_1, RAM_2, RAM_3, RAM_en, Reg_en0, Reg_en1, Reg_en2, Reg_en3;
  wire [3:0] R_0, R_1, R_2, R_3, RAM;

  nand nand_1 (nand_1_out, RAM_en, Clock);
  _74189 _74189_1 (
    .pin1(Adr_0), .pin2(1'b0), .pin3(nand_1_out), .pin4(O_0), .pin5(RAM_0), .pin6(O_1), .pin7(RAM_1),
    .pin8(1'b0), .pin9(RAM_2), .pin10(O_2), .pin11(RAM_3), .pin12(O_3), .pin13(Adr_3), .pin14(Adr_2),
    .pin15(Adr_1), .pin16(1'b1));
  Button button_1 (.out(Clock));
  assign RAM = ~{RAM_3, RAM_2, RAM_1, RAM_0};  // Not not_1, 4 bits wide
  Multiplexer #(.Selector_Bits(3), .Bits(4)) multiplexer_1 (
    .sel({S_2, S_1, S_0}), .in_0(R_0), .in_1(R_1), .in_2(R_2), .in_3(R_3), .in_4(RAM),
    .in_5({I_3, I_2, I_1, I_0}), .in_6({I_3, I_2, I_1, I_0}), .in_7({I_3, I_2, I_1, I_0}),
    .out({O_3, O_2, O_1, O_0}));
  Demultiplexer #(.Selector_Bits(3)) demultiplexer_1 (
    .sel({T_2, T_1, T_0}), .in(1'b1), .out_0(Reg_en0), .out_1(Reg_en1), .out_2(Reg_en2), .out_3(Reg_en3),
    .out_4(RAM_en));  // open: out_5, out_6, out_7
  Register register_1 (.In({O_3, O_2, O_1, O_0}), .Clk(Clock), .En(Reg_en0), .Out(R_0));
  Register register_2 (.In({O_3, O_2, O_1, O_0}), .Clk(Clock), .En(Reg_en1), .Out(R_1));
  Register register_3 (.In({O_3, O_2, O_1, O_0}), .Clk(Clock), .En(Reg_en2), .Out(R_2));
  Register register_4 (.In({O_3, O_2, O_1, O_0}), .Clk(Clock), .En(Reg_en3), .Out(R_3));

  // Other names for the same wires on the sheet: Bus[3:0] = {O_3, O_2, O_1, O_0}; Bus_0 = O_0; Bus_1 = O_1;
  //   Bus_2 = O_2; Bus_3 = O_3; DIN[3:0] = {I_3, I_2, I_1, I_0}; Undef[3:0] = {I_3, I_2, I_1, I_0};
  //   Source[2:0] = {S_2, S_1, S_0}; Sel[2:0] = {T_2, T_1, T_0}
endmodule
