// Digital circuit Register.dig as structural Verilog
module Register (
  input  [3:0] In,
  input  Clk,
  input  En,
  output [3:0] Out
);

  wire multiplexer_1_out;

  Multiplexer multiplexer_1 (.sel(En), .in_0(1'b0), .in_1(Clk), .out(multiplexer_1_out));
  D_FF d_ff_1 (.D(In[0]), .C(multiplexer_1_out), .Q(Out[0]));  // open: nQ
  D_FF d_ff_2 (.D(In[1]), .C(multiplexer_1_out), .Q(Out[1]));  // open: nQ
  D_FF d_ff_3 (.D(In[2]), .C(multiplexer_1_out), .Q(Out[2]));  // open: nQ
  D_FF d_ff_4 (.D(In[3]), .C(multiplexer_1_out), .Q(Out[3]));  // open: nQ

  // Notes on the sheet:
  //   High
endmodule
