// Digital circuit assignment4.dig as structural Verilog
module assignment4 (
  input  D,
  input  C,
  input  B,
  input  A,
  input  X,
  input  Y,
  input  A0,
  input  A1,
  input  A2,
  input  A3,
  input  B0,
  input  B1,
  input  B2,
  input  B3,
  input  plus,
  output Carry,
  output S3,
  output S0,
  output S1,
  output S2
);

  wire _7447_1_pin9, _7447_1_pin10, _7447_1_pin11, _7447_1_pin12, _7447_1_pin13, _7447_1_pin14,
       _7447_1_pin15, _7447_2_pin9, _7447_2_pin10, _7447_2_pin11, _7447_2_pin12, _7447_2_pin13,
       _7447_2_pin14, _7447_2_pin15, add_1_c_o, add_2_c_o, add_3_c_o, and_1_out, nand_1_out, not_1_out,
       not_2_out, not_3_out, not_4_out, or_1_out, or_2_out, xor_1_out;

  not not_1 (not_1_out, B);
  not not_2 (not_2_out, C);
  or or_1 (or_1_out, C, B);
  _7447 _7447_1 (
    .pin1(B), .pin2(C), .pin3(1'b1), .pin4(1'b1), .pin5(1'b1), .pin6(D), .pin7(A), .pin8(1'b0),
    .pin9(_7447_1_pin9), .pin10(_7447_1_pin10), .pin11(_7447_1_pin11), .pin12(_7447_1_pin12),
    .pin13(_7447_1_pin13), .pin14(_7447_1_pin14), .pin15(_7447_1_pin15), .pin16(1'b1));
  nand nand_1 (nand_1_out, D, or_1_out);
  _7447 _7447_2 (
    .pin1(B), .pin2(C), .pin3(1'b1), .pin4(nand_1_out), .pin5(1'b1), .pin6(D), .pin7(A), .pin8(1'b0),
    .pin9(_7447_2_pin9), .pin10(_7447_2_pin10), .pin11(_7447_2_pin11), .pin12(_7447_2_pin12),
    .pin13(_7447_2_pin13), .pin14(_7447_2_pin14), .pin15(_7447_2_pin15), .pin16(1'b1));
  Seven_Seg #(.commonConnectionType("anode"), .commonCathode("true")) seven_seg_1 (
    .a(_7447_1_pin13), .b(_7447_1_pin12), .c(_7447_1_pin11), .d(_7447_1_pin10), .e(_7447_1_pin9),
    .f(_7447_1_pin15), .g(_7447_1_pin14), .dp(1'b1), .common(1'b1));
  Seven_Seg #(.commonCathode("true"), .commonConnectionType("anode")) seven_seg_2 (
    .a(_7447_2_pin13), .b(_7447_2_pin12), .c(_7447_2_pin11), .d(_7447_2_pin10), .e(_7447_2_pin9),
    .f(_7447_2_pin15), .g(_7447_2_pin14), .dp(nand_1_out), .common(1'b1));
  not not_3 (not_3_out, Y);
  or or_2 (or_2_out, X, Y);
  xor xor_1 (xor_1_out, X, Y);
  and and_1 (and_1_out, X, not_3_out);
  not not_4 (not_4_out, xor_1_out);
  Seven_Seg #(.commonConnectionType("anode"), .commonCathode("true")) seven_seg_3 (
    .a(not_3_out), .b(xor_1_out), .c(or_2_out), .d(not_4_out), .e(1'b0), .f(1'b0), .g(and_1_out), .dp(1'b1),
    .common(1'b1));
  Add add_1 (.a(B3), .b(A3), .c_i(1'b0), .s(S0), .c_o(add_1_c_o));
  Add add_2 (.a(B2), .b(A2), .c_i(add_1_c_o), .s(S1), .c_o(add_2_c_o));
  Add add_3 (.a(B1), .b(A1), .c_i(add_2_c_o), .s(S2), .c_o(add_3_c_o));
  Add add_4 (.a(B0), .b(A0), .c_i(add_3_c_o), .s(S3), .c_o(Carry));

  // Notes on the sheet:
  //   0
endmodule
