// Digital circuit assignment41.dig as structural Verilog
module assignment41 (
  input  A0,
  input  A1,
  input  A2,
  input  A3,
  input  B0,
  input  B1,
  input  B2,
  input  B3,
  input  plus,
  output Carry,
  output S0,
  output S3,
  output S2,
  output S1
);

  wire add_1_c_o, add_2_c_o, add_3_c_o, add_4_c_o, xor_1_out, xor_2_out, xor_3_out, xor_4_out;

  xor xor_1 (xor_1_out, plus, B0);
  xor xor_2 (xor_2_out, plus, B1);
  xor xor_3 (xor_3_out, plus, B2);
  xor xor_4 (xor_4_out, plus, B3);
  Add add_1 (.a(A3), .b(xor_4_out), .c_i(plus), .s(S3), .c_o(add_1_c_o));
  Add add_2 (.a(A2), .b(xor_3_out), .c_i(add_1_c_o), .s(S2), .c_o(add_2_c_o));
  Add add_3 (.a(A1), .b(xor_2_out), .c_i(add_2_c_o), .s(S1), .c_o(add_3_c_o));
  Add add_4 (.a(A0), .b(xor_1_out), .c_i(add_3_c_o), .s(S0), .c_o(add_4_c_o));
  xor xor_5 (Carry, plus, add_4_c_o);

  // Notes on the sheet:
  //   0
endmodule
