// Digital circuit 5.2.dig as structural Verilog
module _5_2 (
  input  Y,
  input  X
);

  wire help_decoder_1_a, help_decoder_1_b, help_decoder_1_c, help_decoder_1_d, help_decoder_1_e,
       help_decoder_1_f, help_decoder_1_g;

  HELP_decoder help_decoder_1 (
    .X(X), .Y(Y), .A(help_decoder_1_a), .B(help_decoder_1_b), .C(help_decoder_1_c), .D(help_decoder_1_d),
    .E(help_decoder_1_e), .F(help_decoder_1_f), .G(help_decoder_1_g));
  Seven_Seg #(.commonConnectionType("anode"), .commonCathode("true")) seven_seg_1 (
    .a(help_decoder_1_a), .b(help_decoder_1_b), .c(help_decoder_1_c), .d(help_decoder_1_d),
    .e(help_decoder_1_e), .f(help_decoder_1_f), .g(help_decoder_1_g), .dp(1'b1), .common(1'b1));
endmodule
