// Digital circuit 5.4.dig as structural Verilog
module _5_4 (
  input  C,
  input  B,
  input  A,
  output X,
  output Y
);

  wire _74138_1_pin7, _74138_1_pin10, _74138_1_pin11, _74138_1_pin13, _74138_1_pin14;

  _74138 _74138_1 (
    .pin1(A), .pin2(B), .pin3(C), .pin4(1'b0), .pin5(1'b0), .pin6(1'b1), .pin7(_74138_1_pin7), .pin8(1'b0),
    .pin10(_74138_1_pin10), .pin11(_74138_1_pin11), .pin13(_74138_1_pin13), .pin14(_74138_1_pin14),
    .pin16(1'b1));  // open: pin9, pin12, pin15
  nand nand_1 (Y, _74138_1_pin10, _74138_1_pin13);
  nand nand_2 (X, _74138_1_pin11, _74138_1_pin7, _74138_1_pin14);

  // Notes on the sheet:
  //   2
  //   1
endmodule
