// Digital circuit 5.5.dig as structural Verilog
module _5_5 (
  input  C,
  input  B,
  input  A,
  output A1,
  output A2,
  output B1,
  output B2,
  output C1,
  output C2
);

  wire _74138_1_pin7, _74138_1_pin10, _74138_1_pin11, _74138_1_pin13, _74138_1_pin14, and_1_out, and_2_out,
       and_3_out;

  and and_1 (and_1_out, A, C);
  and and_2 (and_2_out, A, B);
  and and_3 (and_3_out, B, C);
  xor xor_1 (B1, A, B, C);
  Add add_1 (.a(A), .b(B), .c_i(C), .s(C1), .c_o(C2));
  or or_1 (B2, and_1_out, and_2_out, and_3_out);
  _74138 _74138_1 (
    .pin1(A), .pin2(B), .pin3(C), .pin4(1'b0), .pin5(1'b0), .pin6(1'b1), .pin7(_74138_1_pin7), .pin8(1'b0),
    .pin10(_74138_1_pin10), .pin11(_74138_1_pin11), .pin13(_74138_1_pin13), .pin14(_74138_1_pin14),
    .pin16(1'b1));  // open: pin9, pin12, pin15
  nand nand_1 (A2, _74138_1_pin10, _74138_1_pin13);
  nand nand_2 (A1, _74138_1_pin11, _74138_1_pin7, _74138_1_pin14);

  // Notes on the sheet:
  //   2
  //   B == C
  //   1
endmodule
