// Digital circuit HELP_decoder.dig as structural Verilog
module HELP_decoder (
  input  X,
  input  Y,
  output A,
  output B,
  output C,
  output D,
  output E,
  output F,
  output G
);

  not not_1 (A, Y);
  xor xor_1 (B, X, Y);
  or or_1 (C, X, Y);
  and and_1 (G, X, A);
  not not_2 (D, B);

  assign E = 1'b0;
  assign F = 1'b0;
endmodule
