// Digital circuit PSRT1.2.dig as structural Verilog
module PSRT1_2 (
  input  A0,
  input  A1
);

  wire and_2_out, and_3_out, not_1_out, not_2_out, or_1_out;

  not not_1 (not_1_out, A0);
  not not_2 (not_2_out, A1);
  // And and_1 has open pins: In_1=not_1_out, In_2=not_2_out, out=open
  and and_2 (and_2_out, not_2_out, A0);
  and and_3 (and_3_out, A1, not_1_out);
  // And and_4 has open pins: In_1=A1, In_2=A0, out=open
  or or_1 (or_1_out, and_2_out, and_3_out);
  LED S2 (.in(or_1_out));
endmodule
