// Digital circuit CUSTOM_8-1_MUX.dig as structural Verilog
module CUSTOM_8_1_MUX (
  input  i0,
  input  i1,
  input  i2,
  input  i3,
  input  i4,
  input  i5,
  input  i6,
  input  i7,
  input  s0,
  input  s1,
  input  s2,
  output o
);

  wire _74153_1_pin7, _74153_1_pin9, not_1_out;

  not not_1 (not_1_out, s2);
  _74153 _74153_1 (
    .pin1(not_1_out), .pin2(s1), .pin3(i7), .pin4(i6), .pin5(i5), .pin6(i4), .pin7(_74153_1_pin7),
    .pin8(1'b0), .pin9(_74153_1_pin9), .pin10(i0), .pin11(i1), .pin12(i2), .pin13(i3), .pin14(s0),
    .pin15(s2), .pin16(1'b1));
  or or_1 (o, _74153_1_pin9, _74153_1_pin7);
endmodule
