// Digital circuit Part1.dig as structural Verilog
module Part1 (
  input  s0,
  input  s1,
  input  s2,
  output o
);

  wire _74153_1_pin7, _74153_1_pin9, not_1_out;

  not not_1 (not_1_out, s2);
  _74153 _74153_1 (
    .pin1(not_1_out), .pin2(s1), .pin3(1'b0), .pin4(1'b0), .pin5(1'b1), .pin6(1'b0), .pin7(_74153_1_pin7),
    .pin8(1'b0), .pin9(_74153_1_pin9), .pin10(1'b1), .pin11(1'b1), .pin12(1'b1), .pin13(1'b0), .pin14(s0),
    .pin15(s2), .pin16(1'b1));
  or or_1 (o, _74153_1_pin9, _74153_1_pin7);
endmodule
