// Digital circuit Part2.dig as structural Verilog
module Part2 (
  input  C,
  input  B,
  input  A,
  output _1,
  output _2,
  output _3
);

  wire not_1_out;

  not not_1 (not_1_out, B);
  CUSTOM_8_1_MUX custom_8_1_mux_1 (
    .i0(1'b0), .i1(1'b1), .i2(1'b0), .i3(1'b1), .i4(1'b1), .i5(1'b1), .i6(1'b0), .i7(1'b1), .s0(C), .s1(B),
    .s2(A), .o(_1));
  _74153 _74153_1 (
    .pin1(1'b0), .pin2(A), .pin3(C), .pin4(1'b1), .pin5(C), .pin6(C), .pin7(_2), .pin8(1'b0), .pin10(1'b0),
    .pin11(1'b0), .pin12(1'b0), .pin13(1'b0), .pin14(B), .pin15(1'b0), .pin16(1'b1));  // open: pin9
  _74153 _74153_2 (
    .pin1(1'b0), .pin2(A), .pin3(1'b1), .pin4(not_1_out), .pin5(1'b1), .pin6(1'b0), .pin7(_3), .pin8(1'b0),
    .pin10(1'b0), .pin11(1'b0), .pin12(1'b0), .pin13(1'b0), .pin14(C), .pin15(1'b1), .pin16(1'b1));  // open: pin9
endmodule
