// Digital circuit Part4.dig as structural Verilog
module Part4 (
  input  D,
  input  C,
  input  B,
  input  A,
  output wrtD,
  output wrtA,
  output wrtCD,
  output wrtAB
);

  wire and_1_out, not_1_out, not_2_out, not_3_out, not_4_out, or_1_out, xor_1_out;

  not not_1 (not_1_out, D);
  not not_2 (not_2_out, C);
  not not_3 (not_3_out, A);
  CUSTOM_8_1_MUX custom_8_1_mux_1 (
    .i0(not_1_out), .i1(not_1_out), .i2(1'b1), .i3(D), .i4(D), .i5(D), .i6(1'b0), .i7(not_1_out), .s0(C),
    .s1(B), .s2(A), .o(wrtD));
  CUSTOM_8_1_MUX custom_8_1_mux_2 (
    .i0(not_3_out), .i1(A), .i2(not_3_out), .i3(A), .i4(not_3_out), .i5(not_3_out), .i6(A), .i7(not_3_out),
    .s0(D), .s1(C), .s2(B), .o(wrtA));
  xor xor_1 (xor_1_out, B, A);
  not not_4 (not_4_out, xor_1_out);
  _74153 _74153_1 (
    .pin1(1'b0), .pin2(C), .pin3(xor_1_out), .pin4(not_4_out), .pin5(xor_1_out), .pin6(not_3_out),
    .pin7(wrtAB), .pin8(1'b0), .pin10(1'b0), .pin11(1'b0), .pin12(1'b0), .pin13(1'b0), .pin14(D),
    .pin15(1'b0), .pin16(1'b1));  // open: pin9
  and and_1 (and_1_out, C, not_1_out);
  or or_1 (or_1_out, not_2_out, D);
  _74153 _74153_2 (
    .pin1(1'b0), .pin2(A), .pin3(and_1_out), .pin4(D), .pin5(or_1_out), .pin6(not_1_out), .pin7(wrtCD),
    .pin8(1'b0), .pin10(1'b0), .pin11(1'b0), .pin12(1'b0), .pin13(1'b0), .pin14(B), .pin15(1'b0), .pin16(1'b1));  // open: pin9
endmodule
