// Digital circuit Part5.dig as structural Verilog
module Part5 (
  input  I0,
  input  I1,
  input  I2,
  input  I3,
  input  C,
  input  B,
  input  A,
  output o0,
  output o1,
  output o2,
  output o3
);

  CUSTOM_8_1_MUX custom_8_1_mux_1 (
    .i0(I3), .i1(I2), .i2(1'b0), .i3(I0), .i4(I2), .i5(I2), .i6(I3), .i7(1'b0), .s0(C), .s1(B), .s2(A), .o(o3));
  CUSTOM_8_1_MUX custom_8_1_mux_2 (
    .i0(I2), .i1(I1), .i2(I3), .i3(I3), .i4(I1), .i5(I1), .i6(I3), .i7(1'b0), .s0(C), .s1(B), .s2(A), .o(o2));
  CUSTOM_8_1_MUX custom_8_1_mux_3 (
    .i0(I1), .i1(I0), .i2(I2), .i3(I2), .i4(I0), .i5(I0), .i6(I2), .i7(1'b0), .s0(C), .s1(B), .s2(A), .o(o1));
  CUSTOM_8_1_MUX custom_8_1_mux_4 (
    .i0(I0), .i1(1'b0), .i2(I1), .i3(I3), .i4(I3), .i5(1'b0), .i6(I1), .i7(1'b0), .s0(C), .s1(B), .s2(A),
    .o(o0));
endmodule
