// Digital circuit 1.2.dig as structural Verilog
module _1_2 (
  input  S,
  input  EN,
  input  R,
  output Q,
  output nQ
);

  wire nand_1_out, nand_2_out;

  nand nand_1 (nand_1_out, S, EN);
  nand nand_2 (nand_2_out, EN, R);
  nand nand_3 (Q, nand_1_out, nQ);
  nand nand_4 (nQ, Q, nand_2_out);
endmodule
