// Digital circuit 1.3.dig as structural Verilog
module _1_3 (
  input  D,
  input  EN,
  output Q,
  output nQ
);

  wire nand_1_out, nand_2_out, not_1_out;

  not not_1 (not_1_out, D);
  nand nand_1 (nand_1_out, D, EN);
  nand nand_2 (nand_2_out, EN, not_1_out);
  nand nand_3 (Q, nand_1_out, nQ);
  nand nand_4 (nQ, Q, nand_2_out);
endmodule
