// Digital circuit 4.dig as structural Verilog
module _4 (
  input  I0,
  input  I1,
  input  I2,
  input  I3,
  output o0,
  output o1,
  output o2,
  output o3
);

  wire CLK_out;

  Button CLK (.out(CLK_out));
  Dflip_flop dflip_flop_1 (.CLK(CLK_out), .D(I3), .Q(o3));  // open: nQ
  Dflip_flop dflip_flop_2 (.CLK(CLK_out), .D(I2), .Q(o2));  // open: nQ
  Dflip_flop dflip_flop_3 (.CLK(CLK_out), .D(I1), .Q(o1));  // open: nQ
  Dflip_flop dflip_flop_4 (.CLK(CLK_out), .D(I0), .Q(o0));  // open: nQ
endmodule
