// Digital circuit 6.dig as structural Verilog
module _6 (
  input  I0,
  input  I1,
  input  I2,
  input  I3_SIN,
  input  S_L,
  output o3,
  output o2,
  output o1,
  output o0
);

  wire CLK_out, multiplexer_1_out, multiplexer_2_out, multiplexer_3_out;

  Button CLK (.out(CLK_out));
  Dflip_flop dflip_flop_1 (.CLK(CLK_out), .D(I3_SIN), .Q(o3));  // open: nQ
  Multiplexer multiplexer_1 (.sel(S_L), .in_0(o3), .in_1(I2), .out(multiplexer_1_out));
  Dflip_flop dflip_flop_2 (.CLK(CLK_out), .D(multiplexer_1_out), .Q(o2));  // open: nQ
  Multiplexer multiplexer_2 (.sel(S_L), .in_0(o2), .in_1(I1), .out(multiplexer_2_out));
  Dflip_flop dflip_flop_3 (.CLK(CLK_out), .D(multiplexer_2_out), .Q(o1));  // open: nQ
  Multiplexer multiplexer_3 (.sel(S_L), .in_0(o1), .in_1(I0), .out(multiplexer_3_out));
  Dflip_flop dflip_flop_4 (.CLK(CLK_out), .D(multiplexer_3_out), .Q(o0));  // open: nQ
endmodule
