// Digital circuit Dflip-flop.dig as structural Verilog
module Dflip_flop (
  input  CLK,
  input  D,
  output Q,
  output nQ
);

  wire _1_3_1_q, not_1_out;

  not not_1 (not_1_out, CLK);
  _1_3 _1_3_1 (.D(D), .EN(not_1_out), .Q(_1_3_1_q));  // open: nQ
  _1_3 _1_3_2 (.D(_1_3_1_q), .EN(CLK), .Q(Q), .nQ(nQ));
endmodule
