// Digital circuit 1.dig as structural Verilog
module _1 (
  input  X,
  output A,
  output B,
  output C
);

  wire _74175_1_pin9, xor_1_out;

  xor xor_1 (xor_1_out, C, X, B);
  _74175 _74175_1 (
    .pin1(1'b1), .pin2(A), .pin4(xor_1_out), .pin5(A), .pin7(B), .pin8(1'b0), .pin9(_74175_1_pin9),
    .pin10(C), .pin12(B), .pin13(1'b0), .pin16(1'b1));  // open: pin3, pin6, pin11, pin14, pin15
  Button button_1 (.out(_74175_1_pin9));
endmodule
