// Digital circuit 5.dig as structural Verilog
module _5 (
  input  in_5,
  input  in_6,
  input  in_7,
  input  in_8,
  input  in_9,
  input  in_10,
  input  En,
  output out_1,
  output out_2,
  output out_3,
  output out_4
);

  wire button_1_out;

  Regs regs_1 (
    .D_0(in_5), .S_1(in_10), .EN(En), .Clk(button_1_out), .S_0(in_9), .D_1(in_6), .D_2(in_7), .D_3(in_8),
    .O_0(out_1), .O_1(out_2), .O_2(out_3), .O_3(out_4));
  Button button_1 (.out(button_1_out));

  // Notes on the sheet:
  //   Sel
endmodule
