// Digital circuit Regs.dig as structural Verilog
module Regs (
  input  D_0,
  input  S_1,
  input  EN,
  input  Clk,
  input  S_0,
  input  D_1,
  input  D_2,
  input  D_3,
  output O_0,
  output O_1,
  output O_2,
  output O_3
);

  wire multiplexer_1_out, multiplexer_2_out, multiplexer_3_out, multiplexer_4_out;
  wire [3:0] R_0, R_1, R_2, R_3;

  Multiplexer #(.Selector_Bits(3)) multiplexer_1 (
    .sel({EN, S_0, S_1}), .in_0(1'b0), .in_1(1'b0), .in_2(1'b0), .in_3(1'b0), .in_4(Clk), .in_5(1'b0),
    .in_6(1'b0), .in_7(1'b0), .out(multiplexer_1_out));
  Multiplexer #(.Selector_Bits(3)) multiplexer_2 (
    .sel({EN, S_0, S_1}), .in_0(1'b0), .in_1(1'b0), .in_2(1'b0), .in_3(1'b0), .in_4(1'b0), .in_5(Clk),
    .in_6(1'b0), .in_7(1'b0), .out(multiplexer_2_out));
  Multiplexer #(.Selector_Bits(3)) multiplexer_3 (
    .sel({EN, S_0, S_1}), .in_0(1'b0), .in_1(1'b0), .in_2(1'b0), .in_3(1'b0), .in_4(1'b0), .in_5(1'b0),
    .in_6(Clk), .in_7(1'b0), .out(multiplexer_3_out));
  Multiplexer #(.Selector_Bits(3)) multiplexer_4 (
    .sel({EN, S_0, S_1}), .in_0(1'b0), .in_1(1'b0), .in_2(1'b0), .in_3(1'b0), .in_4(1'b0), .in_5(1'b0),
    .in_6(1'b0), .in_7(Clk), .out(multiplexer_4_out));
  D_FF d_ff_1 (.D(D_3), .C(multiplexer_1_out), .Q(R_3[0]));  // open: nQ
  D_FF d_ff_2 (.D(D_2), .C(multiplexer_1_out), .Q(R_3[1]));  // open: nQ
  D_FF d_ff_3 (.D(D_1), .C(multiplexer_1_out), .Q(R_3[2]));  // open: nQ
  D_FF d_ff_4 (.D(D_0), .C(multiplexer_1_out), .Q(R_3[3]));  // open: nQ
  D_FF d_ff_5 (.D(D_3), .C(multiplexer_2_out), .Q(R_2[0]));  // open: nQ
  D_FF d_ff_6 (.D(D_2), .C(multiplexer_2_out), .Q(R_2[1]));  // open: nQ
  D_FF d_ff_7 (.D(D_1), .C(multiplexer_2_out), .Q(R_2[2]));  // open: nQ
  D_FF d_ff_8 (.D(D_0), .C(multiplexer_2_out), .Q(R_2[3]));  // open: nQ
  D_FF d_ff_9 (.D(D_3), .C(multiplexer_3_out), .Q(R_1[0]));  // open: nQ
  D_FF d_ff_10 (.D(D_2), .C(multiplexer_3_out), .Q(R_1[1]));  // open: nQ
  D_FF d_ff_11 (.D(D_1), .C(multiplexer_3_out), .Q(R_1[2]));  // open: nQ
  D_FF d_ff_12 (.D(D_0), .C(multiplexer_3_out), .Q(R_1[3]));  // open: nQ
  D_FF d_ff_13 (.D(D_3), .C(multiplexer_4_out), .Q(R_0[0]));  // open: nQ
  D_FF d_ff_14 (.D(D_2), .C(multiplexer_4_out), .Q(R_0[1]));  // open: nQ
  D_FF d_ff_15 (.D(D_1), .C(multiplexer_4_out), .Q(R_0[2]));  // open: nQ
  D_FF d_ff_16 (.D(D_0), .C(multiplexer_4_out), .Q(R_0[3]));  // open: nQ
  Multiplexer #(.Selector_Bits(3)) multiplexer_5 (
    .sel({EN, S_0, S_1}), .in_0(R_3[0]), .in_1(R_2[0]), .in_2(R_1[0]), .in_3(R_0[0]), .in_4(1'b0),
    .in_5(1'b0), .in_6(1'b0), .in_7(1'b0), .out(O_3));
  Multiplexer #(.Selector_Bits(3)) multiplexer_6 (
    .sel({EN, S_0, S_1}), .in_0(R_3[1]), .in_1(R_2[1]), .in_2(R_1[1]), .in_3(R_0[1]), .in_4(1'b0),
    .in_5(1'b0), .in_6(1'b0), .in_7(1'b0), .out(O_2));
  Multiplexer #(.Selector_Bits(3)) multiplexer_7 (
    .sel({EN, S_0, S_1}), .in_0(R_3[2]), .in_1(R_2[2]), .in_2(R_1[2]), .in_3(R_0[2]), .in_4(1'b0),
    .in_5(1'b0), .in_6(1'b0), .in_7(1'b0), .out(O_1));
  Multiplexer #(.Selector_Bits(3)) multiplexer_8 (
    .sel({EN, S_0, S_1}), .in_0(R_3[3]), .in_1(R_2[3]), .in_2(R_1[3]), .in_3(R_0[3]), .in_4(1'b0),
    .in_5(1'b0), .in_6(1'b0), .in_7(1'b0), .out(O_0));

  // Other names for the same wires on the sheet: Clock = Clk; In[3:0] = {D_0, D_1, D_2, D_3};
  //   Sel[2:0] = {EN, S_0, S_1}

  // Notes on the sheet:
  //   High
endmodule
