// Digital circuit 1.dig as structural Verilog
module _1 (
  input  X,
  output Y
);

  wire A_q, and_1_out, and_2_out, and_3_out, and_4_out, B_nq, B_q, button_1_out, C_nq, C_q, not_1_out,
       or_1_out, or_2_out, xor_1_out;

  not not_1 (not_1_out, X);
  and and_1 (and_1_out, not_1_out, B_q, C_q);
  xor xor_1 (xor_1_out, B_q, C_q);
  and and_2 (and_2_out, B_nq, not_1_out);
  and and_3 (and_3_out, B_q, C_nq);
  or or_1 (or_1_out, A_q, xor_1_out);
  or or_2 (or_2_out, and_2_out, and_3_out);
  and and_4 (and_4_out, or_1_out, X);
  Button button_1 (.out(button_1_out));
  D_FF A (.D(and_1_out), .C(button_1_out), .Q(A_q));  // open: nQ
  D_FF B (.D(and_4_out), .C(button_1_out), .Q(B_q), .nQ(B_nq));
  D_FF C (.D(or_2_out), .C(button_1_out), .Q(C_q), .nQ(C_nq));
  LED led_1 (.in(A_q));
  LED led_2 (.in(B_q));
  LED led_3 (.in(C_q));
  and and_5 (Y, A_q, not_1_out);

  // Notes on the sheet:
  //   ~X*B*C
  //   B X C
  //   ~X*~B
  //   B*~C
  //   ~X*A
endmodule
