// Digital circuit Register.dig as structural Verilog
module Register (
  input  [3:0] In,
  input  Clk,
  input  En,
  output [3:0] Out
);

  wire multiplexer_1_out;
  wire [3:0] d_ff_1_q;

  Multiplexer multiplexer_1 (.sel(En), .in_0(1'b0), .in_1(Clk), .out(multiplexer_1_out));
  D_FF d_ff_1 (.D(In[0]), .C(multiplexer_1_out), .Q(d_ff_1_q[0]));  // open: nQ
  D_FF d_ff_2 (.D(In[1]), .C(multiplexer_1_out), .Q(d_ff_1_q[1]));  // open: nQ
  D_FF d_ff_3 (.D(In[2]), .C(multiplexer_1_out), .Q(d_ff_1_q[2]));  // open: nQ
  D_FF d_ff_4 (.D(In[3]), .C(multiplexer_1_out), .Q(d_ff_1_q[3]));  // open: nQ
  Multiplexer #(.Bits(4)) multiplexer_2 (.sel(En), .in_0(d_ff_1_q), .in_1(4'b0000), .out(Out));

  // Notes on the sheet:
  //   High
endmodule
