// Digital circuit Regs.dig as structural Verilog
module Regs (
  input  I_0,
  input  T_1,
  input  EN,
  input  T_0,
  input  I_1,
  input  I_2,
  input  I_3,
  input  S_0,
  input  S_1,
  input  S_2,
  output O_0,
  output O_1,
  output O_2,
  output O_3
);

  wire Clock, demultiplexer_1_out_0, demultiplexer_1_out_1, demultiplexer_1_out_2, demultiplexer_1_out_3;
  wire [3:0] Bus, R_0, R_1, R_2, R_3;

  Multiplexer #(.Selector_Bits(3), .Bits(4)) multiplexer_1 (
    .sel({S_0, S_1, S_2}), .in_0(R_0), .in_1(R_1), .in_2(R_2), .in_3(R_3), .in_4({I_0, I_1, I_2, I_3}),
    .in_5({I_0, I_1, I_2, I_3}), .in_6({I_0, I_1, I_2, I_3}), .in_7({I_0, I_1, I_2, I_3}), .out(Bus));
  Button button_1 (.out(Clock));
  Demultiplexer #(.Selector_Bits(2)) demultiplexer_1 (
    .sel({T_1, T_0}), .in(EN), .out_0(demultiplexer_1_out_0), .out_1(demultiplexer_1_out_1),
    .out_2(demultiplexer_1_out_2), .out_3(demultiplexer_1_out_3));
  Multiplexer #(.Selector_Bits(2)) multiplexer_2 (
    .sel({T_1, T_0}), .in_0(R_0[3]), .in_1(R_1[3]), .in_2(R_2[3]), .in_3(R_3[3]), .out(O_0));
  Multiplexer #(.Selector_Bits(2)) multiplexer_3 (
    .sel({T_1, T_0}), .in_0(R_0[2]), .in_1(R_1[2]), .in_2(R_2[2]), .in_3(R_3[2]), .out(O_1));
  Multiplexer #(.Selector_Bits(2)) multiplexer_4 (
    .sel({T_1, T_0}), .in_0(R_0[1]), .in_1(R_1[1]), .in_2(R_2[1]), .in_3(R_3[1]), .out(O_2));
  Multiplexer #(.Selector_Bits(2)) multiplexer_5 (
    .sel({T_1, T_0}), .in_0(R_0[0]), .in_1(R_1[0]), .in_2(R_2[0]), .in_3(R_3[0]), .out(O_3));
  Register register_1 (.In(Bus), .Clk(Clock), .En(demultiplexer_1_out_0), .Out(R_0));
  Register register_2 (.In(Bus), .Clk(Clock), .En(demultiplexer_1_out_1), .Out(R_1));
  Register register_3 (.In(Bus), .Clk(Clock), .En(demultiplexer_1_out_2), .Out(R_2));
  Register register_4 (.In(Bus), .Clk(Clock), .En(demultiplexer_1_out_3), .Out(R_3));

  // Other names for the same wires on the sheet: DIN[3:0] = {I_0, I_1, I_2, I_3}; Undef[3:0] = {I_0, I_1, I_2, I_3};
  //   Source[2:0] = {S_0, S_1, S_2}; Sel[1:0] = {T_1, T_0}
endmodule
